# Fritzing sketch layer (saved by Fritzing 0.9.0b)
circuit board: 12.876cm x 11.663cm
breadboards: 1

parts:
  U1 = atmega328 [package=dip]
  CT1 = Crystal [frequency="16 Mhz" package=THT]
  C1 = Ceramic Capacitor [capacitance=100nF package="100 mil [THT, multilayer]"]
  C2 = Ceramic Capacitor [capacitance=100nF package="100 mil [THT, multilayer]"]
  S1 = Pushbutton [package="[THT]"]
  R1 = Resistor [tolerance=±5% resistance=220 package=THT]
  gnd = Pad [width=3.07728581910459 height=2.9373266949429 connect=center]
  vcc = Pad [width=3.07728581910459 height=2.9373266949429 connect=center]
  R3 = Resistor [tolerance=±5% resistance=220 package=THT]
  Pad1 = Pad [width=2.68687104585827 height=2.74211930831974 connect=center]
  Pad2 = Pad [width=2.68687104585827 height=2.74211930831974 connect=center]
  vcc_2 = Pad [width=2.68687104585827 height=2.74211930831974 connect=center]
  gnd_2 = Pad [width=2.68687104585827 height=2.74211930831974 connect=center]
  D1 = Rectifier Diode [part_number=1N4001 package="300 mil [THT]"]
  T1 = TRANSISTOR_NPN [package=to-92-ammo]
  Pad3 = Pad [width=2.68687104585827 height=2.74211930831974 connect=center]
  Pad4 = Pad [width=2.68687104585827 height=2.74211930831974 connect=center]
  S4 = Pad [width=2.68687104585827 height=2.74211930831974 connect=center]
  Pad5 = Pad [width=2.68687104585827 height=2.74211930831974 connect=center]
  S3 = Pad [width=2.68687104585827 height=2.74211930831974 connect=center]
  Pad6 = Pad [width=2.68687104585827 height=2.74211930831974 connect=center]
  S2 = Pad [width=2.68687104585827 height=2.74211930831974 connect=center]
  S1_2 = Pad [width=2.68687104585827 height=2.74211930831974 connect=center]
  Pad7 = Pad [width=2.68687104585827 height=2.74211930831974 connect=center]
  S5 = Pad [width=2.68687104585827 height=2.74211930831974 connect=center]
  Pad8 = Pad [width=2.68687104585827 height=2.74211930831974 connect=center]
  S6 = Pad [width=2.68687104585827 height=2.74211930831974 connect=center]
  Pad9 = Pad [width=2.68687104585827 height=2.74211930831974 connect=center]
  A = Pad [width=2.68687104585827 height=2.74211930831974 connect=center]
  LED1 = LED - 5mm [color="Red (633nm)" package="5 mm [THT]"]
  R4 = Resistor [tolerance=±5% resistance=220 package=THT]
  Pad10 = Pad [width=2.68687104585827 height=2.74211930831974 connect=center]
  Pad11 = Pad [width=2.68687104585827 height=2.74211930831974 connect=center]
  Pad12 = Pad [width=2.68687104585827 height=2.74211930831974 connect=center]
  Pad13 = Pad [width=2.68687104585827 height=2.74211930831974 connect=center]
  vcc_3 = Pad [width=2.68687104585827 height=2.74211930831974 connect=center]  # not connected
  gnd_3 = Pad [width=2.68687104585827 height=2.74211930831974 connect=center]
  vcc_4 = Pad [width=2.68687104585827 height=2.74211930831974 connect=center]
  vcc_5 = Basic FET P-Channel [package="TO220 [THT]"]
  part = Electrolytic Capacitor [capacitance=1µF package="100 mil [THT, electrolytic]"]
  C4 = Electrolytic Capacitor [capacitance=1µF package="100 mil [THT, electrolytic]"]
  gnd_4 = Pad [width=2.68687104585827 height=2.74211930831974 connect=center]

nets:
  N1: U1.RESET, R1.Pin_1
  N2: U1.VCC, S1.Pin_3, S1.Pin_4, R1.Pin_0, vcc.pad, Pad3.pad, Pad8.pad, Pad9.pad
  N3: U1.GND#7, C1.1, C2.0, S1.Pin_1, S1.Pin_2, gnd.pad, gnd_2.pad, T1.C, LED1.cathode
  N4: U1.XLAT1, CT1.pin_0, C2.1
  N5: U1.XLAT2, CT1.pin_1, C1.0
  N6: U1.D9_(PWM), R3.Pin_0
  N7: U1.D10_(PWM), S1_2.pad
  N8: U1.D11_(PWM), S2.pad
  N9: U1.D12, S3.pad
  N10: U1.D13, S4.pad
  N11: U1.AVCC, vcc_2.pad, D1.cathode, Pad4.pad, Pad5.pad, Pad6.pad, Pad7.pad, R4.Pin_1, Pad12.pad, vcc_5.source, part.+
  N12: U1.A0, S5.pad
  N13: U1.A1, S6.pad
  N14: U1.A2, A.pad
  N15: R3.Pin_1, T1.B
  N16: Pad1.pad, Pad10.pad
  N17: Pad2.pad, Pad13.pad
  N18: D1.anode, T1.E, Pad11.pad
  N19: LED1.anode, R4.Pin_0
  N20: gnd_3.pad, vcc_5.drain, part.-, C4.-, gnd_4.pad
  N21: vcc_4.pad, vcc_5.gate, C4.+
